# Fritzing sketch Beer_opener_schematic (saved by Fritzing 1.0.4)
breadboards: 1

parts:
  Part1 = Arduino Uno (Rev3)
  VCC1 = 4 x AAA Battery Mount [internal_resistance=0.1Ω]
  S1 = Pushbutton [package="[SMD]"]
  R1 = Resistor [tolerance=±5% resistance=10k package="2010 [SMD]"]
  M1 = fc-51 [package=THT]
  J1 = Basic Servo

nets:
  N1: Part1.D8, S1.Pin_1, S1.Pin_2, R1.Pin_1
  N2: Part1.D9_PWM, J1.pulse
  N3: Part1.D2, M1.pin1
  GND: Part1.GND, VCC1.-, R1.Pin_0, M1.pin2, J1.gnd
  VIN: Part1.VIN, VCC1.+, S1.Pin_3, S1.Pin_4, M1.pin3, J1.vcc
