# Fritzing sketch ControlLEDWithPotmeter (saved by Fritzing 1.0.4)
breadboards: 1

parts:
  V1 = DC Power [voltage=5V internal_resistance=0.1Ω]
  LED1 = LED - 5mm [color="Red (633nm)" current=0.030A package="5 mm [THT]"]
  R1 = Rotary Potentiometer (Small) [maximum_resistance=10kΩ knob_status=50% power=0.5W package=THT]
  R2 = Resistor [tolerance=±5% power=0.25W resistance=220 package=THT]

nets:
  N1: V1.V-, R2.Pin_0
  N2: V1.V+, R1.leg2
  N3: LED1.cathode, R2.Pin_1
  N4: LED1.anode, R1.leg1
