# Fritzing sketch Exercise1 (saved by Fritzing 1.0.4)
breadboards: 1

parts:
  V1 = DC Power [voltage=5V internal_resistance=0.1Ω]
  R1 = Resistor [tolerance=±5% power=0.25W resistance=220 package=THT]
  VM1 = Multimeter (DC Voltage)
  AM1 = Multimeter (DC Current)

nets:
  N1: V1.V-, AM1.COM_Probe
  N2: V1.V+, R1.Pin_0, VM1.V_Probe
  N3: R1.Pin_1, VM1.COM_Probe, AM1.A_Probe
