# Fritzing sketch Exercise1current (saved by Fritzing 1.0.4)
breadboards: 1

parts:
  V1 = DC Power [voltage=5V internal_resistance=0.1Ω]
  R1 = Resistor [tolerance=±5% power=0.25W resistance=220 package=THT]
  AM1 = Multimeter (DC Current)

nets:
  GND: V1.V-, AM1.COM_Probe
  N1: V1.V+, R1.Pin_0
  N2: R1.Pin_1, AM1.A_Probe
