# Fritzing sketch Exercise2resistors (saved by Fritzing 1.0.4)
breadboards: 1

parts:
  R1 = Resistor [tolerance=±5% power=0.25W resistance=10k package=THT]
  R2 = Resistor [tolerance=±5% power=0.25W resistance=10k package=THT]
  OM1 = Multimeter (Ohmmeter)
  OM2 = Multimeter (Ohmmeter)
  R3 = Resistor [tolerance=±5% power=0.25W resistance=10k package=THT]
  R4 = Resistor [tolerance=±5% power=0.25W resistance=10k package=THT]

nets:
  N1: R1.Pin_0, OM1.V_Probe
  N2: R1.Pin_1, R2.Pin_0
  N3: R2.Pin_1, OM1.COM_Probe
  N4: OM2.COM_Probe, R3.Pin_1, R4.Pin_1
  N5: OM2.V_Probe, R3.Pin_0, R4.Pin_0
