# Fritzing sketch Exercise2voltagedivider (saved by Fritzing 1.0.4)
breadboards: 1

parts:
  R1 = Resistor [tolerance=±5% power=0.25W resistance=220 package=THT]
  R2 = Resistor [tolerance=±5% power=0.25W resistance=220 package=THT]
  VCC1 = 4 x AAA Battery Mount [internal_resistance=0.1Ω]
  VM1 = Multimeter (DC Voltage)

nets:
  N1: R1.Pin_0, VCC1.-
  N2: R1.Pin_1, R2.Pin_0, VM1.COM_Probe
  N3: R2.Pin_1, VCC1.+, VM1.V_Probe
