# Fritzing sketch MA5 (saved by Fritzing 1.0.4)
breadboards: 7

parts:
  VCC4 = 4 x AAA Battery Mount [internal_resistance=0.1Ω]
  R10 = Rotary Potentiometer (Small) [maximum_resistance=10kΩ knob_status=50% power=0.5W package=THT]
  VM5 = Multimeter (DC Voltage)
  VCC5 = 4 x AAA Battery Mount [internal_resistance=0.1Ω]
  S1 = Pushbutton [package="[THT]"]
  R12 = Resistor [tolerance=±5% power=0.25W resistance=220 package=THT]
  VM4 = Multimeter (DC Voltage)
  S2 = Pushbutton [package="[THT]"]
  VCC6 = 4 x AAA Battery Mount [internal_resistance=0.1Ω]
  R11 = Resistor [tolerance=±5% power=0.25W resistance=220 package=THT]
  LED2 = LED - 5mm [color="Red (633nm)" current=0.030A package="5 mm [THT]"]
  VM3 = Multimeter (DC Voltage)
  R2 = Resistor [tolerance=±5% power=0.25W resistance=220 package=THT]
  R8 = Resistor [tolerance=±5% power=0.25W resistance=10k package=THT]
  OM2 = Multimeter (Ohmmeter)
  VM2 = Multimeter (DC Voltage)
  VCC3 = 4 x AAA Battery Mount [internal_resistance=0.1Ω]
  OM1 = Multimeter (Ohmmeter)
  VCC1 = 4 x AAA Battery Mount [internal_resistance=0.1Ω]
  R4 = Resistor [tolerance=±5% power=0.25W resistance=10k package=THT]
  R9 = Resistor [tolerance=±5% power=0.25W resistance=10k package=THT]
  R6 = Resistor [tolerance=±5% power=0.25W resistance=10k package=THT]
  VM1 = Multimeter (DC Voltage)
  R5 = Resistor [tolerance=±5% power=0.25W resistance=10k package=THT]
  R7 = Resistor [tolerance=±5% power=0.25W resistance=10k package=THT]
  AM1 = Multimeter (DC Current)
  R1 = Rotary Potentiometer (Small) [maximum_resistance=10kΩ knob_status=0% power=0.5W package=THT]
  R3 = Resistor [tolerance=±5% power=0.25W resistance=220 package=THT]
  LED1 = LED - 5mm [color="Red (633nm)" current=0.030A package="5 mm [THT]"]
  VCC2 = 4 x AAA Battery Mount [internal_resistance=0.1Ω]

nets:
  N1: VCC4.-, R10.wiper, VM5.COM_Probe
  N2: VCC4.+, R10.leg1, VM5.V_Probe
  N3: VCC5.-, R11.Pin_1
  N4: VCC5.+, S1.Pin_1, S1.Pin_2, VM3.V_Probe
  N5: S1.Pin_3, S1.Pin_4, R11.Pin_0, VM3.COM_Probe
  N6: R12.Pin_0, VCC6.-
  N7: R12.Pin_1, LED2.cathode
  N8: VM4.COM_Probe, S2.Pin_3, S2.Pin_4, LED2.anode
  N9: VM4.V_Probe, S2.Pin_1, S2.Pin_2, VCC6.+
  N10: R2.Pin_0, VCC1.-
  N11: R2.Pin_1, LED1.cathode
  N12: R8.Pin_0, VCC3.-
  N13: R8.Pin_1, VM2.COM_Probe, R9.Pin_0
  N14: OM2.COM_Probe, R6.Pin_0
  N15: OM2.V_Probe, R7.Pin_1
  N16: VM2.V_Probe, VCC3.+, R9.Pin_1
  N17: OM1.COM_Probe, R4.Pin_0, R5.Pin_0
  N18: OM1.V_Probe, R4.Pin_1, R5.Pin_1
  N19: VCC1.+, R1.wiper
  N20: R6.Pin_1, R7.Pin_0
  N21: VM1.COM_Probe, AM1.A_Probe, R3.Pin_1
  N22: VM1.V_Probe, R3.Pin_0, VCC2.+
  N23: AM1.COM_Probe, VCC2.-
  N24: R1.leg1, LED1.anode
