# Fritzing sketch ReadPotmeter (saved by Fritzing 1.0.4)
breadboards: 1

parts:
  R1 = Rotary Potentiometer (Small) [maximum_resistance=1kΩ knob_status=70% power=0.5W package=THT]
  V1 = DC Power [voltage=5V internal_resistance=0.1Ω]
  VM1 = Multimeter (DC Voltage)

nets:
  N1: R1.leg1, V1.V+, VM1.V_Probe
  N2: R1.wiper, VM1.COM_Probe
  N3: R1.leg2, V1.V-
