# Fritzing sketch ReadStatusOfSwitch (saved by Fritzing 1.0.4)
breadboards: 1

parts:
  R1 = Resistor [tolerance=±5% power=0.25W resistance=220 package=THT]
  V1 = DC Power [voltage=5V internal_resistance=0.1Ω]
  VM1 = Multimeter (DC Voltage)
  S1 = Pushbutton [package=THT]

nets:
  N1: R1.Pin_0, VM1.V_Probe, S1.leg1
  N2: R1.Pin_1, V1.V-, VM1.COM_Probe
  N3: V1.V+, S1.leg0
