# Fritzing sketch SwitchLED (saved by Fritzing 1.0.4)
breadboards: 1

parts:
  V1 = DC Power [voltage=5V internal_resistance=0.1Ω]
  LED1 = LED - 5mm [color="Red (633nm)" current=0.030A package="5 mm [THT]"]
  S1 = Pushbutton [package=THT]
  R1 = Resistor [tolerance=±5% power=0.25W resistance=10k package=THT]

nets:
  N1: V1.V-, R1.Pin_0
  N2: V1.V+, S1.leg1
  N3: LED1.cathode, R1.Pin_1
  N4: LED1.anode, S1.leg0
