# Fritzing sketch MA7 (saved by Fritzing 1.0.4)
breadboards: 3

parts:
  U1 = atmega328 [package=dip]
  R1 = Resistor [tolerance=±5% power=0.25W resistance=470 package=THT]
  LED1 = LED - 5mm [color="Red (633nm)" current=0.030A package="5 mm [THT]"]
  R2 = Resistor [tolerance=±5% power=0.25W resistance=10k package=THT]
  R3 = Resistor [tolerance=±5% power=0.25W resistance=470 package=THT]
  LED2 = LED - 5mm [color="Red (633nm)" current=0.030A package="5 mm [THT]"]
  C1 = Ceramic Capacitor [capacitance=22pF voltage=35V package="100 mil [THT, multilayer]"]
  Part1 = Arduino Ethernet Shield (Rev3)
  R4 = Resistor [tolerance=±5% power=0.25W resistance=220 package=THT]
  LED3 = LED - 5mm [color="Red (633nm)" current=0.030A package="5 mm [THT]"]
  S1 = Pushbutton [package=THT]
  R5 = Resistor [tolerance=±5% power=0.25W resistance=10k package=THT]
  Part2 = Arduino Ethernet Shield (Rev3)
  R6 = Rotary Potentiometer (Small) [maximum_resistance=10kΩ knob_status=50% power=0.5W package=THT]

nets:
  RESET: U1.RESET, R2.Pin_0
  ATMEGA 5V: U1.VCC, U1.AVCC, R2.Pin_1, C1.1
  GND: U1.GND, LED1.cathode, LED2.cathode, C1.0, Part1.GND, LED3.cathode, S1.leg1, Part2.GND, R6.leg1
  13: U1.D7, R1.Pin_0
  14: U1.D8, R3.Pin_0
  N1: R1.Pin_1, LED1.anode
  N2: R3.Pin_1, LED2.anode
  5V: Part1.PWM_D11, R5.Pin_1
  BTN IN: Part1.SPI/D12, S1.leg0, R5.Pin_0
  13 OUT: Part1.SPI/D13, R4.Pin_1
  N3: R4.Pin_0, LED3.anode
  5V 2: Part2.SPI/D13, R6.leg2
  POT IN: Part2.A0, R6.wiper
