# Fritzing sketch ir_to_motor (saved by Fritzing 1.0.4)
breadboards: 2

parts:
  VCC1 = 4 x AAA Battery Mount [internal_resistance=0.1Ω]
  VM1 = Multimeter (DC Voltage)
  M2 = DC Motor [voltage_(max)=6V voltage_(min)=3V]
  Q1 = NPN-Transistor [package="TO92 [THT]"]
  Q2 = NPN-Transistor [package="TO92 [THT]"]
  R1 = Resistor [tolerance=±5% power=0.25W resistance=10k package=THT]
  R2 = Resistor [tolerance=±5% power=0.25W resistance=150 package=THT]
  Q3 = NPN-Transistor [package="TO92 [THT]"]
  M4 = DC Motor [voltage_(max)=6V voltage_(min)=3V]
  VCC2 = 4 x AAA Battery Mount [internal_resistance=0.1Ω]
  M3 = fc-51 [package=THT]
  M1 = fc-51 [package=THT]

nets:
  N1: VCC1.-, VM1.COM_Probe, Q2.E, M1.pin2
  N2: VCC1.+, M2.pin_1, M1.pin3
  N3: VM1.V_Probe, R1.Pin_1, M1.pin1
  N4: M2.pin_2, Q1.C, Q2.C
  N5: Q1.E, Q2.B
  N6: Q1.B, R1.Pin_0
  N7: R2.Pin_0, Q3.B
  N8: R2.Pin_1, M3.pin1
  N9: Q3.E, VCC2.-, M3.pin2
  N10: Q3.C, M4.pin_2
  N11: M4.pin_1, VCC2.+, M3.pin3
